# Fritzing sketch Master_Pi (saved by Fritzing 0.9.2b)

parts:
  A1 = Raspberry Pi 5  # not connected
  Back = L298N DC motor driver
  Part1 = Adafruit PCA9685 PWM/Servo Breakout [part_number=815]  # not connected
  J2 = Basic Servo  # not connected
  U1 = HC-SR04 [chip_label=IC package="SIP (Single Inline) [THT]"]  # not connected
  U2 = LIPO-2000mAh [package=lipo-2000]  # not connected
  M3 = DC Motor
  M4 = DC Motor
  J3 = Basic Servo  # not connected
  J4 = Basic Servo  # not connected
  J5 = Basic Servo  # not connected
  J6 = Basic Servo  # not connected

nets:
  N1: Back.OUT1, M3.pin_1
  N2: Back.OUT2, M3.pin_2
  GND: Back.GND
  N3: Back.OUT3, M4.pin_2
  N4: Back.OUT4, M4.pin_1

custom parts:
  Raspberry Pi 5: The RPi5, a faster version of the awesome Raspberry Pi4B ARM Board with 40 pin gpio.
  L298N DC motor driver: 2x DC motor driver with 78M05 positive voltage regulator (7..35 V) L298N: max 46 V, 2 A Set 5 V Enable jumper to enable 5 V regultor (needed for the L298N) and +5 V output at screw terminal or supply external +5 V at screw terminal Set ENA and/or ENB to +5 V to enable motor permanently or supply ENA and/or ENB with PWM signal IN1 and IN2 set rotation directory for motor A (OUT1/OUT2) IN2 and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
  Adafruit PCA9685 PWM/Servo Breakout: Using only two pins, control 16 free-running PWM outputs! I2C-controlled PWM driver with a built in clock. Unlike the TLC5940 family, you do not need to continuously send it signal tying up your microcontroller, its completely free running! 5V compliant, which means you can control it from a 3.3V microcontroller and still safely drive up to 6V outputs (this is good for when you want to control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
  HC-SR04: HC-SR04 ultrasound distance sensor
